# Fritzing sketch collar_schematic (saved by Fritzing 0.9.3b)

parts:
  Heltec_Wireless_Stick_Lite1 = Heltec Wireless Stick Lite [part_number=HTIT-WSL]
  Part1 = Arduino Nano 33 BLE Sense
  Part2 = u-blox NEO-6M GPS Breakout
  BAT1 = 18650 battery holder [package=battery-18650-kit]
  BAT2 = 18650 battery holder [package=battery-18650-kit]
  IC1 = Voltage Regulator AMS1117 [package=sot223]
  C1 = Capacitor Polarized [package=panasonic_c]

nets:
  N1: Heltec_Wireless_Stick_Lite1.pin_14, Part1.TX
  GND: Heltec_Wireless_Stick_Lite1.pin_18, Heltec_Wireless_Stick_Lite1.pin_22, Part1.GND, Part1.A7, Part2.GND, BAT2.-, IC1.GND, C1.-
  N2: Heltec_Wireless_Stick_Lite1.pin_19, Part2.VCC
  N3: Heltec_Wireless_Stick_Lite1.pin_20, Part1.VIN, IC1.OUT, C1.+
  N4: Heltec_Wireless_Stick_Lite1.pin_23, Part2.TXD
  N5: Heltec_Wireless_Stick_Lite1.pin_28, Part2.RXD
  N6: BAT1.+, IC1.IN
  N7: BAT1.-, BAT2.+

notes:
  AMS1171
  5V Regulator
  Two batteries put on series to produce ~8V
  10μF capacitor
  Arduino Nano BLE Sense

custom parts:
  Heltec Wireless Stick Lite: Wireless Stick Lite is a part of the Heltec LoRa series and incorporates an ESP32-Pico processor, WiFi, LoRa and Bluetooth with an integrated CP2102 USB to serial port interface and onboard SHT1.25 battery interface with integrated lithium battery management system.
  Arduino Nano 33 BLE Sense: The Nano 33 BLE Sense (without headers) is Arduino’s 3.3V AI enabled board in the smallest available form factor: 45x18mm! The Arduino Nano 33 BLE Sense is a completely new board on a well-known form factor. It comes with a series of embedded sensors: 9 axis inertial sensor: what makes this board ideal for wearable devices humidity, and temperature sensor: to get highly accurate measurements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
  18650 battery holder: 18650 Battery Holder
